# Fritzing sketch Esquematico_Blink (saved by Fritzing 1.0.5)
breadboards: 1

parts:
  R1 = Resistor [tolerance=±5% power=0.25W resistance=220 package=THT]
  LED1 = LED - 5mm [color="Red (633nm)" current=0.030A package="5 mm [THT]"]  # not connected
  Componente1 = Arduino Uno (Rev3)

nets:
  N1: R1.Pin_1, Componente1.D13/SCK

// code stored in the sketch: Blink.ino
const int pinLED = 13;  // Pin 13 es el LED integrado en la mayoría de Arduino

void setup() {
  pinMode(pinLED, OUTPUT);
}

void loop() {
  digitalWrite(pinLED, HIGH);   
  delay(1000);                       
  digitalWrite(pinLED, LOW);    
  delay(1000);                      
}
